# Fritzing sketch standard_finish (saved by Fritzing 0.9.6b)
breadboards: 1

parts:
  Part1 = Arduino Uno (Rev3) - ICSP
  U1 = Sharp PC817 [package=THT]
  R1 = Resistor [tolerance=±5% resistance=1500 package="1206 [SMD]"]
  Power_plug1 = Power plug
  J1 = Dagu DGServo 9g header (male) [package=THT]

nets:
  N1: Part1.D7, U1.Pin_4
  N2: Part1.GND, U1.Pin_3
  N3: U1.Pin_1, R1.Pin_0
  GND: U1.Pin_2, Power_plug1.GND, J1.gnd
  N4: R1.Pin_1, J1.pulse
  VCC: Power_plug1.VCC, J1.Vcc

notes:
  E3Z NPN Sensor
  12V power source
  1,5K ohm
